# Fritzing sketch d1_led (saved by Fritzing 0.9.3b)
breadboards: 1

parts:
  WeMos_D1_Mini1 = WeMos D1 Mini
  R1 = Resistor [tolerance=±5% resistance=220 package=THT]
  LED1 = LED - 5mm [color="Red (633nm)" package="5 mm [THT]"]

nets:
  N1: WeMos_D1_Mini1.D2, R1.Pin_0
  N2: WeMos_D1_Mini1.G, LED1.cathode
  N3: R1.Pin_1, LED1.anode
