# Fritzing sketch RGB_led (saved by Fritzing 0.9.3b)
breadboards: 1

parts:
  LED1 = RGB LED - (4 legs) [package="5 mm [THT]"]
  WeMos_D1_Mini1 = WeMos D1 Mini
  R1 = Resistor [tolerance=±5% resistance=220 package=THT]
  R2 = Resistor [tolerance=±5% resistance=220 package=THT]
  R3 = Resistor [tolerance=±5% resistance=220 package=THT]

nets:
  N1: LED1.red_cathode, R1.Pin_1
  N2: LED1.common_anode, WeMos_D1_Mini1.3V3
  N3: LED1.green_cathode, R3.Pin_1
  N4: LED1.blue_cathode, R2.Pin_0
  N5: WeMos_D1_Mini1.D5, R1.Pin_0
  N6: WeMos_D1_Mini1.D6, R3.Pin_0
  N7: WeMos_D1_Mini1.D7, R2.Pin_1
