# Fritzing sketch lcd_relay (saved by Fritzing 0.9.3b)
breadboards: 1

parts:
  WeMos_D1_Mini1 = WeMos D1 Mini
  LCD2 = LCD screen
  LCM1602_IIC2 = LCM1602 IIC [part_number="LCM1602 IIC" chip_label="LCM1602 IIC" package="DIP (Dual Inline) [THT]"]
  KY-2 = Keyes Relay [package=THT]

nets:
  5V: WeMos_D1_Mini1.5V, LCM1602_IIC2.VCC, KY-2.power
  N1: WeMos_D1_Mini1.D0, KY-2.signal
  N2: WeMos_D1_Mini1.D1, LCM1602_IIC2.SCL
  N3: WeMos_D1_Mini1.D2, LCM1602_IIC2.SDA
  N4: WeMos_D1_Mini1.G, LCM1602_IIC2.GND, KY-2.ground
  VSS: LCD2.VSS, LCM1602_IIC2.VSS
  VDD: LCD2.VDD, LCM1602_IIC2.VDD
  N5: LCD2.V0, LCM1602_IIC2.V0
  N6: LCD2.RS, LCM1602_IIC2.RS
  N7: LCD2.R/W, LCM1602_IIC2.RW
  N8: LCD2.E, LCM1602_IIC2.E
  N9: LCD2.DB0, LCM1602_IIC2.D0
  N10: LCD2.DB1, LCM1602_IIC2.D1
  N11: LCD2.DB2, LCM1602_IIC2.D2
  N12: LCD2.DB3, LCM1602_IIC2.D3
  N13: LCD2.DB4, LCM1602_IIC2.D4
  N14: LCD2.DB5, LCM1602_IIC2.D5
  N15: LCD2.DB6, LCM1602_IIC2.D6
  N16: LCD2.DB7, LCM1602_IIC2.D7
  N17: LCD2.LED+, LCM1602_IIC2.A
  N18: LCD2.LED-, LCM1602_IIC2.K

notes:
  in1是黃色線

custom parts:
  LCM1602 IIC: I2C-Module to use a 1602 or 2004 LCD on with the wire.h libory Serial LCD Modul
  Keyes Relay: The Keyes 5V relay module is suitable for SCM development, home appliance control. It uses a 5V~12V TIL control signal which can control DC / AC signal.
