# Fritzing sketch home (saved by Fritzing 0.9.3b)
breadboards: 1

parts:
  WeMos_D1_Mini1 = WeMos D1 Mini
  S1 = Reed switch [package=THT]
  HTU21D-F1 = Adafruit HTU21D-F Temperature & Humidity Sensor Breakout Board
  元件1 = Breakout Board for Electret Microphone

nets:
  3V3: WeMos_D1_Mini1.3V3, HTU21D-F1.3v3
  5V: WeMos_D1_Mini1.5V, 元件1.VCC
  N1: WeMos_D1_Mini1.A0, 元件1.AUD
  N2: WeMos_D1_Mini1.D1, HTU21D-F1.SCL
  N3: WeMos_D1_Mini1.D2, HTU21D-F1.SDA
  N4: WeMos_D1_Mini1.D8, S1.pin_1
  GND: WeMos_D1_Mini1.G, S1.pin_2, HTU21D-F1.GND, 元件1.GND

notes:
  磁簧開關
  HTU21D-溫度,濕度
  I2C
  聲音感測器
