# Fritzing sketch Untitled Sketch (saved by Fritzing 0.9.3b)
breadboards: 1

parts:
  WeMos_D1_Mini1 = WeMos D1 Mini
  T1 = LM35 Temperature Sensor [package="TO92 [THT]"]
  U5 = 74HC595 [package="DIP16 [THT]"]
  U1 = 7-SEGMENT-4DIGIT [package=7-segment-4digit]

nets:
  5V: WeMos_D1_Mini1.5V, T1.+Vs, U5.MR, U5.VCC
  N1: WeMos_D1_Mini1.A0, T1.Vout
  N2: WeMos_D1_Mini1.D1, U1.8
  N3: WeMos_D1_Mini1.D2, U1.11
  N4: WeMos_D1_Mini1.D3, U1.13
  N5: WeMos_D1_Mini1.D4, U1.16
  N6: WeMos_D1_Mini1.D5, U5.DS
  N7: WeMos_D1_Mini1.D6, U5.ST_CP
  N8: WeMos_D1_Mini1.D7, U5.SH_CP
  GND: WeMos_D1_Mini1.G, T1.GND, U5.GND, U5.OE
