# Fritzing sketch AnalogInputPot (saved by Fritzing 0.9.2b)
circuit board: 6.88566cm x 5.36311cm
breadboards: 1

parts:
  可變電阻 = Rotary Potentiometer (Small) [maximum_resistance=10k package=THT]
  Arduino2 = Arduino Uno (Rev3)

nets:
  N1: 可變電阻.leg1, Arduino2.GND
  N2: 可變電阻.wiper, Arduino2.A3
  N3: 可變電阻.leg2, Arduino2.5V

// code stored in the sketch: AnalogInputPot.ino
/*
  AnalogReadSerial
  Reads an analog input on pin 0, prints the result to the serial monitor.
  Graphical representation is available using serial plotter (Tools > Serial Plotter menu)
  Attach the center pin of a potentiometer to pin A0, and the outside pins to +5V and ground.

  This example code is in the public domain.
*/

// the setup routine runs once when you press reset:
void setup() {
  // initialize serial communication at 9600 bits per second:
  Serial.begin(9600);
}

// the loop routine runs over and over again forever:
void loop() {
  // read the input on analog pin 0:
  int sensorValue = analogRead(A3);
  // print out the value you read:
  Serial.println(sensorValue);
  delay(1);        // delay in between reads for stability
}
