# Fritzing sketch relay_button (saved by Fritzing 0.9.3b)
breadboards: 1

parts:
  WeMos_D1_Mini1 = WeMos D1 Mini
  S2 = Pushbutton [package="[THT]"]
  R1 = Resistor [tolerance=±5% resistance=10k package=THT]

nets:
  N1: WeMos_D1_Mini1.5V, S2.Pin_1, S2.Pin_2
  N2: WeMos_D1_Mini1.D1, S2.Pin_3, S2.Pin_4, R1.Pin_1
  N3: WeMos_D1_Mini1.G, R1.Pin_0

notes:
  5v,GND
  IN1—連接 Arduino 擴充板的 Digital Pin 4
