# Fritzing sketch AnalogInputOutput (saved by Fritzing 0.9.3b)
circuit board: 6.88566cm x 5.36311cm
breadboards: 2

parts:
  R4 = Resistor [resistance=220 tolerance=±5% package=THT]
  LED2 = LED - 5mm [color="Red (633nm)" package="5 mm [THT]"]
  R3 = Rotary Potentiometer (Small) [maximum_resistance=100kΩ package=THT]
  Arduino2 = Arduino Uno (Rev3)

nets:
  N1: R4.Pin_0, LED2.anode
  N2: R4.Pin_1, Arduino2.D3_PWM
  N3: LED2.cathode, R3.leg2, Arduino2.GND
  N4: R3.leg1, Arduino2.5V
  N5: R3.wiper, Arduino2.A3

notes:
  In this example, potentiometer values are read in through an 'Analog In' pin. The values are then used to control the modulation of an LED on a PWM pin. Related examples: http://arduino.cc/en/Tutorial/AnalogInput http://arduino.cc/en/Tutorial/Fading

// code stored in the sketch: AnalogInputOptput.ino

#define led 3
#define potentiometer A3

void setup() {
  pinMode(potentiometer,INPUT);
  pinMode(led,OUTPUT);
  Serial.begin(9600);
}

void loop() {
  int inputValue = analogRead(potentiometer);
  int outputValue = (float)inputValue / 1023 * 255;
  Serial.println(outputValue);
  analogWrite(led,outputValue);

}
