# Fritzing sketch switch1 (saved by Fritzing 0.9.3b)
circuit board: 6.88566cm x 5.36311cm
breadboards: 2

parts:
  R4 = Resistor [resistance=220 tolerance=±5% package=THT]
  R3 = Resistor [resistance=220 tolerance=±5% package=THT]
  R2 = Resistor [resistance=220 tolerance=±5% package=THT]
  R5 = Resistor [resistance=220 tolerance=±5% package=THT]
  R6 = Resistor [resistance=220 tolerance=±5% package=THT]
  LED3 = LED - 5mm [color="Red (633nm)" package="5 mm [THT]"]
  LED6 = LED - 5mm [color="Red (633nm)" package="5 mm [THT]"]
  LED2 = LED - 5mm [color="Red (633nm)" package="5 mm [THT]"]
  LED5 = LED - 5mm [color="Red (633nm)" package="5 mm [THT]"]
  LED4 = LED - 5mm [color="Red (633nm)" package="5 mm [THT]"]
  Arduino = Arduino Uno (Rev3)

nets (from the schematic view):
  N1: R4.Pin_0, LED4.anode
  N2: R4.Pin_1, Arduino.D5_PWM
  N3: R3.Pin_0, LED3.anode
  N4: R3.Pin_1, Arduino.D4
  N5: R2.Pin_0, LED2.anode
  N6: R2.Pin_1, Arduino.D3_PWM
  N7: R5.Pin_0, LED5.anode
  N8: R5.Pin_1, Arduino.D6_PWM
  N9: R6.Pin_0, LED6.anode
  N10: R6.Pin_1, Arduino.D7
  N11: LED3.cathode, LED6.cathode, LED2.cathode, LED5.cathode, LED4.cathode, Arduino.GND

// code stored in the sketch: arrays.ino
/*
  Arrays

 Demonstrates the use of  an array to hold pin numbers
 in order to iterate over the pins in a sequence.
 Lights multiple LEDs in sequence, then in reverse.

 Unlike the For Loop tutorial, where the pins have to be
 contiguous, here the pins can be in any random order.

 The circuit:
 * LEDs from pins 2 through 7 to ground

 created 2006
 by David A. Mellis
 modified 30 Aug 2011
 by Tom Igoe

This example code is in the public domain.

 http://www.arduino.cc/en/Tutorial/Array
 */

int timer = 100;           // The higher the number, the slower the timing.
int ledPins[] = {
  2, 7, 4, 6, 5, 3
};       // an array of pin numbers to which LEDs are attached
int pinCount = 6;           // the number of pins (i.e. the length of the array)

void setup() {
  // the array elements are numbered from 0 to (pinCount - 1).
  // use a for loop to initialize each pin as an output:
  for (int thisPin = 0; thisPin < pinCount; thisPin++) {
    pinMode(ledPins[thisPin], OUTPUT);
  }
}

void loop() {
  // loop from the lowest pin to the highest:
  for (int thisPin = 0; thisPin < pinCount; thisPin++) {
    // turn the pin on:
    digitalWrite(ledPins[thisPin], HIGH);
    delay(timer);
    // turn the pin off:
    digitalWrite(ledPins[thisPin], LOW);

  }

  // loop from the highest pin to the lowest:
  for (int thisPin = pinCount - 1; thisPin >= 0; thisPin--) {
    // turn the pin on:
    digitalWrite(ledPins[thisPin], HIGH);
    delay(timer);
    // turn the pin off:
    digitalWrite(ledPins[thisPin], LOW);
  }
}

// code stored in the sketch: Loop.ino
/*
  For Loop Iteration
 
 Demonstrates the use of a for() loop. 
 Lights multiple LEDs in sequence, then in reverse.
 
 The circuit:
 * LEDs from pins 2 through 7 to ground
 
 created 2006
 by David A. Mellis
 modified 30 Aug 2011
 by Tom Igoe 

This example code is in the public domain.
 
 http://www.arduino.cc/en/Tutorial/ForLoop
 */

int timer = 100;           // The higher the number, the slower the timing.

void setup() {
  // use a for loop to initialize each pin as an output:
  for (int thisPin = 2; thisPin < 8; thisPin++)  {
    pinMode(thisPin, OUTPUT);      
  }
}

void loop() {
  // loop from the lowest pin to the highest:
  for (int thisPin = 2; thisPin < 8; thisPin++) { 
    // turn the pin on:
    digitalWrite(thisPin, HIGH);   
    delay(timer);                  
    // turn the pin off:
    digitalWrite(thisPin, LOW);    
  }

  // loop from the highest pin to the lowest:
  for (int thisPin = 7; thisPin >= 2; thisPin--) { 
    // turn the pin on:
    digitalWrite(thisPin, HIGH);
    delay(timer);
    // turn the pin off:
    digitalWrite(thisPin, LOW);
  }
}

// code stored in the sketch: switch1.ino
/*
  Switch statement  with serial input

 Demonstrates the use of a switch statement.  The switch
 statement allows you to choose from among a set of discrete values
 of a variable.  It's like a series of if statements.

 To see this sketch in action, open the Serial monitor and send any character.
 The characters a, b, c, d, and e, will turn on LEDs.  Any other character will turn
 the LEDs off.

 The circuit:
 * 5 LEDs attached to digital pins 2 through 6 through 220-ohm resistors

 created 1 Jul 2009
 by Tom Igoe

This example code is in the public domain.

 http://www.arduino.cc/en/Tutorial/SwitchCase2
 */

void setup() {
  // initialize serial communication:
  Serial.begin(9600);
  // initialize the LED pins:
  for (int thisPin = 2; thisPin < 7; thisPin++) {
    pinMode(thisPin, OUTPUT);
  }
}

void loop() {
  // read the sensor:
  if (Serial.available() > 0) {
    int inByte = Serial.read();
    // do something different depending on the character received.
    // The switch statement expects single number values for each case;
    // in this exmaple, though, you're using single quotes to tell
    // the controller to get the ASCII value for the character.  For
    // example 'a' = 97, 'b' = 98, and so forth:

    switch (inByte) {
      case 'a':
        digitalWrite(2, HIGH);
        break;
      case 'b':
        digitalWrite(3, HIGH);
        break;
      case 'c':
        digitalWrite(4, HIGH);
        break;
      case 'd':
        digitalWrite(5, HIGH);
        break;
      case 'e':
        digitalWrite(6, HIGH);
        break;
      default:
        // turn all the LEDs off:
        for (int thisPin = 2; thisPin < 7; thisPin++) {
          digitalWrite(thisPin, LOW);
        }
    }
  }
}
